// Logisim project RV32I.circ as structural Verilog: 1 circuit, main circuit main
module main (
);

  wire [2:0] instructiondecoder_1_funct3, instructiondecoder_1_type;
  wire [4:0] instructiondecoder_1_rd, instructiondecoder_1_rs1, instructiondecoder_1_rs2;
  wire [6:0] instructiondecoder_1_funct7;
  wire [11:0] instructiondecoder_1_iimm, instructiondecoder_1_simm;
  wire [12:0] instructiondecoder_1_bimm;
  wire [20:0] instructiondecoder_1_jimm;
  wire [31:0] instructiondecoder_1_uimm;

  // RegFile_main main_1: pin names not known
  // ALU_main main_2: pin names not known
  // Probe on instructiondecoder_1_type
  InstructionDecoder instructiondecoder_1 (
    .rd(instructiondecoder_1_rd), .funct3(instructiondecoder_1_funct3), .rs1(instructiondecoder_1_rs1),
    .rs2(instructiondecoder_1_rs2), .funct7(instructiondecoder_1_funct7), .IImm(instructiondecoder_1_iimm),
    .SImm(instructiondecoder_1_simm), .BImm(instructiondecoder_1_bimm), .UImm(instructiondecoder_1_uimm),
    .JImm(instructiondecoder_1_jimm), .\type (instructiondecoder_1_type));  // open: Instruction
  // Probe on instructiondecoder_1_rd
  // Probe on instructiondecoder_1_funct3
  // Probe on instructiondecoder_1_rs1
  // Probe on instructiondecoder_1_rs2
  // Probe on instructiondecoder_1_funct7
  // Probe on instructiondecoder_1_iimm
  // Probe on instructiondecoder_1_simm
  // Probe on instructiondecoder_1_bimm
  // Probe on instructiondecoder_1_uimm
  // Probe on instructiondecoder_1_jimm
  RAM #(.addrWidth(24)) ram_1 ();  // open: addr, data, sel, clk, ld, clr
endmodule
